# Fritzing sketch FRITZING_DIAGRAM (saved by Fritzing 0.9.3b)

parts:
  Mod1 = zmpt101b
  Part1 = Current Sensor 5A
  U1 = ESP32-38PinWide [part_number=ESP32-38PinWide]
  M1 = AC-05-03
  J1 = Terminal Block - 3 pins [package=THT]
  J2 = Terminal Block - 3 pins [package=THT]
  o1 = Module display OLED I2C 128x64 SSD1306 [package=THT]

nets:
  N1: Mod1.OUT, U1.GPIO34
  N2: Part1.1, J1.Line_1
  N3: Part1.2, Part1.OUT, U1.GPIO36, J2.Line_1
  N4: U1.GPIO11, M1.pin_4
  N5: U1.VIN, M1.pin_3
  N6: U1.GPIO21, o1.SDA
  N7: U1.GPIO22, o1.SCL
  N8: J1.Line_2, J2.Line_2
  N9: J1.Line_3, J2.Line_3

custom parts:
  zmpt101b: Single phase ac active output voltate transformer module.
  ESP32-38PinWide: Generic 38-Pin ESP32 with wide format (only access to one side of pins on a breadboard) based on Stephen Lilley's HiLetgo ESP-WROOM-32 ESP32 ESP-32S Development Board.
  AC-05-03: AC-DC 220V to 5V Step-Down Power Supply Module
  Terminal Block - 3 pins: Generic Screw Terminal 8mm
  Module display OLED I2C 128x64 SSD1306: Ecran OLED I2C SSD163 de 128x64 avec connexion I2C
